// Logisim project bb0.2.circ as structural Verilog: 20 circuits, main circuit main
// 0xf
module main (
  input  Clear,
  output [7:0] out_2,
  output [7:0] out_3,
  output [7:0] out_4,
  output [7:0] out_5,
  output [7:0] out_6,
  output [3:0] PCMonitor,
  output [7:0] Jump_Register
);

  wire ALU_cout, clock_1_out, controlled_buffer_1_out, controlled_buffer_3_out, controlled_buffer_5_out,
       controlled_buffer_7_out, counter_1_q, decoder_1_out1, not_1_out, not_2_out, not_3_out, not_4_out,
       not_5_out, not_6_out, xor_1_out;
  wire [3:0] LC_q, SC_q;
  wire [7:0] OutputReg_ledout, programcounter_1_busout, rom_1_data;
  wire [11:6] CPU_out_3_2;
  wire [25:0] CPU_out_3;
  wire [31:0] decimaldecoder_1_out_2;

  assign controlled_buffer_1_out = not_4_out ? 1'b1 : 1'bz;  // Controlled_Buffer controlled_buffer_1
  not not_1 (not_1_out, controlled_buffer_7_out);
  assign controlled_buffer_1_out = controlled_buffer_3_out ? not_2_out : 1'bz;  // Controlled_Buffer controlled_buffer_2
  not not_2 (not_2_out, CPU_out_3[15]);
  assign controlled_buffer_3_out = not_3_out ? 1'b0 : 1'bz;  // Controlled_Buffer controlled_buffer_3
  not not_3 (not_3_out, xor_1_out);
  assign controlled_buffer_3_out = xor_1_out ? 1'b1 : 1'bz;  // Controlled_Buffer controlled_buffer_4
  not not_4 (not_4_out, CPU_out_3[15]);
  Counter #(.width(4), .max('hf)) SC (
    .count(controlled_buffer_1_out), .Q(SC_q), .clk(not_1_out), .clr(controlled_buffer_5_out));  // open: load, D, carry
  xor xor_1 (xor_1_out, decoder_1_out1, CPU_out_3[15]);
  assign controlled_buffer_5_out = CPU_out_3[12] ? controlled_buffer_7_out : 1'bz;  // Controlled_Buffer controlled_buffer_5
  CPU CPU (
    .InstructionCounter(SC_q), .InstructionIn(out_5[7:4]),
    .out_3({CPU_out_3[25:6], CPU_out_3_2, CPU_out_3[5:0]}));
  ProgramCounter programcounter_1 (
    .Enable(CPU_out_3[7]), .Load(CPU_out_3[8]), .DIn(Jump_Register[3:0]), .Count(CPU_out_3[10]),
    .Clock(controlled_buffer_7_out), .Clear(Clear), .BusOut(programcounter_1_busout), .MonitorOut(PCMonitor));
  Decoder #(.disabled(0), .enable("false")) decoder_1 (.out1(decoder_1_out1), .sel(counter_1_q));  // open: out0
  Counter #(.width(4), .max('hf)) LC (
    .count(CPU_out_3[13]), .Q(LC_q), .clk(controlled_buffer_7_out));  // open: load, D, carry, clr
  LED led_1 (.in(programcounter_1_busout[7]));
  LED led_2 (.in(programcounter_1_busout[6]));
  LED led_3 (.in(programcounter_1_busout[4]));
  LED led_4 (.in(programcounter_1_busout[5]));
  Counter #(.width(1), .max('h1)) counter_1 (
    .count(CPU_out_3[15]), .Q(counter_1_q), .clk(controlled_buffer_7_out), .clr(not_5_out));  // open: load, D, carry
  not not_5 (not_5_out, CPU_out_3[15]);
  assign programcounter_1_busout = CPU_out_3[14] ? {LC_q, LC_q} : 8'bz;  // Controlled_Buffer controlled_buffer_6
  LED led_5 (.in(programcounter_1_busout[0]));
  LED led_6 (.in(programcounter_1_busout[1]));
  LED led_7 (.in(programcounter_1_busout[3]));
  LED led_8 (.in(programcounter_1_busout[2]));
  Clock clock_1 (.out(clock_1_out));
  not not_6 (not_6_out, CPU_out_3[9]);
  assign controlled_buffer_7_out = not_6_out ? clock_1_out : 1'bz;  // Controlled_Buffer controlled_buffer_7
  IFUnit ifunit_1 (
    .RoutWrite(CPU_out_3[17]), .DataIn(programcounter_1_busout), .CandWrite(CPU_out_3[19]),
    .CompWrite(CPU_out_3[18]), .Clock(controlled_buffer_7_out), .IfOut(CPU_out_3[20]),
    .AddrOut(programcounter_1_busout));
  LED led_9 (.in(OutputReg_ledout[7]));
  LED led_10 (.in(OutputReg_ledout[6]));
  _8REG OutputReg (
    .Clock(controlled_buffer_7_out), .Load(CPU_out_3[6]), .Data(programcounter_1_busout),
    .LEDOut(OutputReg_ledout));  // open: Enable, DOut
  _8REG u_8reg_1 (
    .Clock(controlled_buffer_7_out), .Load(CPU_out_3[16]), .Data(programcounter_1_busout), .Enable(1'b0),
    .LEDOut(Jump_Register));  // open: DOut
  _8REG MAR (
    .Clock(controlled_buffer_7_out), .Load(CPU_out_3[5]), .Data(programcounter_1_busout),
    .Enable(CPU_out_3[4]), .LEDOut(out_3), .DOut(programcounter_1_busout));
  _8REG InstructionReg (
    .Clock(controlled_buffer_7_out), .Load(CPU_out_3[1]), .Data(programcounter_1_busout),
    .Enable(CPU_out_3[0]), .LEDOut(out_5), .DOut(programcounter_1_busout));
  LED led_11 (.in(OutputReg_ledout[4]));
  LED led_12 (.in(OutputReg_ledout[3]));
  LED led_13 (.in(OutputReg_ledout[2]));
  LED led_14 (.in(OutputReg_ledout[5]));
  LED led_15 (.in(OutputReg_ledout[0]));
  LED led_16 (.in(OutputReg_ledout[1]));
  _7_Segment_Display u_7_segment_display_1 (
    .g(decimaldecoder_1_out_2[15]), .f(decimaldecoder_1_out_2[14]), .a(decimaldecoder_1_out_2[13]),
    .b(decimaldecoder_1_out_2[12]), .e(decimaldecoder_1_out_2[31]), .d(decimaldecoder_1_out_2[30]),
    .c(decimaldecoder_1_out_2[29]), .dp(decimaldecoder_1_out_2[28]));
  DecimalDecoder decimaldecoder_1 (.Data(OutputReg_ledout), .out_2(decimaldecoder_1_out_2));
  _16RAM RAM (
    .Clock(controlled_buffer_7_out), .Data_In(programcounter_1_busout), .Write(CPU_out_3[3]),
    .Address(out_3[3:0]), .Enable(CPU_out_3[2]), .BusOut(programcounter_1_busout));  // open: out_7, out_8, out_9, out_10, out_11, out_12, out_13, out_14, out_15, out_16, out_17, out_18, out_19, out_20, out_21, out_22
  _7_Segment_Display u_7_segment_display_2 (
    .g(decimaldecoder_1_out_2[11]), .f(decimaldecoder_1_out_2[10]), .a(decimaldecoder_1_out_2[9]),
    .b(decimaldecoder_1_out_2[8]), .e(decimaldecoder_1_out_2[27]), .d(decimaldecoder_1_out_2[26]),
    .c(decimaldecoder_1_out_2[25]), .dp(decimaldecoder_1_out_2[24]));
  _7_Segment_Display u_7_segment_display_3 (
    .g(decimaldecoder_1_out_2[7]), .f(decimaldecoder_1_out_2[6]), .a(decimaldecoder_1_out_2[5]),
    .b(decimaldecoder_1_out_2[4]), .e(decimaldecoder_1_out_2[23]), .d(decimaldecoder_1_out_2[22]),
    .c(decimaldecoder_1_out_2[21]), .dp(decimaldecoder_1_out_2[20]));
  _8REG RegA (
    .Clock(controlled_buffer_7_out), .Load(CPU_out_3_2[11]), .Data(programcounter_1_busout),
    .Enable(CPU_out_3_2[10]), .LEDOut(out_2), .DOut(programcounter_1_busout));
  _8REG RegB (
    .Clock(controlled_buffer_7_out), .Load(CPU_out_3_2[9]), .Data(programcounter_1_busout),
    .Enable(CPU_out_3_2[8]), .LEDOut(out_4), .DOut(programcounter_1_busout));
  ALU ALU (
    .A(out_2), .B(out_4), .Enable(CPU_out_3_2[7]), .Subtract(CPU_out_3_2[6]), .AddMonitor(out_6),
    .Sum(programcounter_1_busout), .COut(ALU_cout));
  _7_Segment_Display u_7_segment_display_4 (
    .g(decimaldecoder_1_out_2[3]), .f(decimaldecoder_1_out_2[2]), .a(decimaldecoder_1_out_2[1]),
    .b(decimaldecoder_1_out_2[0]), .e(decimaldecoder_1_out_2[19]), .d(decimaldecoder_1_out_2[18]),
    .c(decimaldecoder_1_out_2[17]), .dp(decimaldecoder_1_out_2[16]));
  OverflowReg OFU (
    .Overflow(ALU_cout), .Write(CPU_out_3[21]), .Enable(CPU_out_3[22]), .Clock(controlled_buffer_7_out),
    .AddrIn(programcounter_1_busout), .AddrOut(programcounter_1_busout));
  assign programcounter_1_busout = CPU_out_3[11] ? rom_1_data : 8'bz;  // Controlled_Buffer controlled_buffer_8
  ROM #(.addrWidth(4)) rom_1 (.addr(out_3[7:4]), .data(rom_1_data));  // open: sel

  // Notes on the sheet:
  //   Program Counter
  //   Bus Monitor
  //   IF
  //   HDD
  //   contents of rom_1 (hex, n*v repeats v):
  //   3e 4f 50 7e 60 10*0 1
endmodule

module _8REG (
  input  Clock,
  input  Load,
  input  [7:0] Data,
  input  Enable,
  output [7:0] LEDOut,
  output [7:0] DOut
);

  _1REG u_1reg_1 (.Clock(Clock), .Load(Load), .Data(Data[0]), .Q(LEDOut[0]));
  _1REG u_1reg_2 (.Clock(Clock), .Load(Load), .Data(Data[1]), .Q(LEDOut[1]));
  _1REG u_1reg_3 (.Clock(Clock), .Load(Load), .Data(Data[2]), .Q(LEDOut[2]));
  _1REG u_1reg_4 (.Clock(Clock), .Load(Load), .Data(Data[3]), .Q(LEDOut[3]));
  _1REG u_1reg_5 (.Clock(Clock), .Load(Load), .Data(Data[4]), .Q(LEDOut[4]));
  _1REG u_1reg_6 (.Clock(Clock), .Load(Load), .Data(Data[5]), .Q(LEDOut[5]));
  _1REG u_1reg_7 (.Clock(Clock), .Load(Load), .Data(Data[6]), .Q(LEDOut[6]));
  _1REG u_1reg_8 (.Clock(Clock), .Load(Load), .Data(Data[7]), .Q(LEDOut[7]));
  assign DOut[0] = Enable ? LEDOut[0] : 1'bz;  // Controlled_Buffer controlled_buffer_1
  assign DOut[1] = Enable ? LEDOut[1] : 1'bz;  // Controlled_Buffer controlled_buffer_2
  assign DOut[2] = Enable ? LEDOut[2] : 1'bz;  // Controlled_Buffer controlled_buffer_3
  assign DOut[3] = Enable ? LEDOut[3] : 1'bz;  // Controlled_Buffer controlled_buffer_4
  assign DOut[4] = Enable ? LEDOut[4] : 1'bz;  // Controlled_Buffer controlled_buffer_5
  assign DOut[5] = Enable ? LEDOut[5] : 1'bz;  // Controlled_Buffer controlled_buffer_6
  assign DOut[6] = Enable ? LEDOut[6] : 1'bz;  // Controlled_Buffer controlled_buffer_7
  assign DOut[7] = Enable ? LEDOut[7] : 1'bz;  // Controlled_Buffer controlled_buffer_8
endmodule

module SRLATCH (
  input  R,
  input  S,
  output Q,
  output nQ
);

  nor nor_1 (Q, R, nQ);
  nor nor_2 (nQ, Q, S);
endmodule

module DLATCH (
  input  Enable,
  input  D,
  output Q,
  output nQ
);

  wire and_1_out, and_2_out, not_1_out;

  not not_1 (not_1_out, D);
  and and_1 (and_1_out, not_1_out, Enable);
  and and_2 (and_2_out, Enable, D);
  SRLATCH srlatch_1 (.R(and_1_out), .S(and_2_out), .Q(Q), .nQ(nQ));
endmodule

module _1REG (
  input  Clock,
  input  Load,
  input  Data,
  output Q
);

  wire and_1_out, and_2_out, not_1_out, or_1_out;

  not not_1 (not_1_out, Load);
  and and_1 (and_1_out, Q, not_1_out);
  and and_2 (and_2_out, Load, Data);
  or or_1 (or_1_out, and_1_out, and_2_out);
  D_Flip_Flop d_ff_1 (.clk(Clock), .D(or_1_out), .Q(Q));  // open: Qn, preset, en, reset
endmodule

module BusInEnable (
  input  [7:0] DIN,
  input  Enable,
  output [7:0] DOUT
);

  assign DOUT[0] = Enable ? DIN[0] : 1'bz;  // Controlled_Buffer controlled_buffer_1
  assign DOUT[1] = Enable ? DIN[1] : 1'bz;  // Controlled_Buffer controlled_buffer_2
  assign DOUT[2] = Enable ? DIN[2] : 1'bz;  // Controlled_Buffer controlled_buffer_3
  assign DOUT[3] = Enable ? DIN[3] : 1'bz;  // Controlled_Buffer controlled_buffer_4
  assign DOUT[4] = Enable ? DIN[4] : 1'bz;  // Controlled_Buffer controlled_buffer_5
  assign DOUT[5] = Enable ? DIN[5] : 1'bz;  // Controlled_Buffer controlled_buffer_6
  assign DOUT[6] = Enable ? DIN[6] : 1'bz;  // Controlled_Buffer controlled_buffer_7
  assign DOUT[7] = Enable ? DIN[7] : 1'bz;  // Controlled_Buffer controlled_buffer_8
endmodule

module _1BitAdd (
  input  A,
  input  B,
  input  CIn,
  output Sum,
  output COut
);

  wire and_1_out, and_2_out, xor_1_out;

  and and_1 (and_1_out, B, A);
  xor xor_1 (xor_1_out, A, B);
  and and_2 (and_2_out, CIn, xor_1_out);
  xor xor_2 (Sum, xor_1_out, CIn);
  or or_1 (COut, and_2_out, and_1_out);
endmodule

module ALU (
  input  [7:0] A,
  input  Subtract,
  input  [7:0] B,
  input  Enable,
  output [7:0] AddMonitor,
  output [7:0] Sum,
  output COut
);

  wire n4bitadd_1_cout;
  wire [7:0] inverter_1_dout;

  Inverter inverter_1 (.DIn(B), .Enable(Subtract), .DOut(inverter_1_dout));
  _4BitAdd u_4bitadd_1 (
    .CIn(Subtract), .A(A[3:0]), .B(inverter_1_dout[3:0]), .Sum(AddMonitor[3:0]), .COut(n4bitadd_1_cout));
  _4BitAdd u_4bitadd_2 (
    .CIn(n4bitadd_1_cout), .A(A[7:4]), .B(inverter_1_dout[7:4]), .Sum(AddMonitor[7:4]), .COut(COut));
  BusInEnable businenable_1 (.DIN(AddMonitor), .Enable(Enable), .DOUT(Sum));
endmodule

module _4BitAdd (
  input  CIn,
  input  [3:0] A,
  input  [3:0] B,
  output [3:0] Sum,
  output COut
);

  wire n1bitadd_1_cout, n1bitadd_2_cout, n1bitadd_3_cout;

  _1BitAdd u_1bitadd_1 (.A(A[0]), .B(B[0]), .CIn(CIn), .Sum(Sum[0]), .COut(n1bitadd_1_cout));
  _1BitAdd u_1bitadd_2 (.A(A[1]), .B(B[1]), .CIn(n1bitadd_1_cout), .Sum(Sum[1]), .COut(n1bitadd_2_cout));
  _1BitAdd u_1bitadd_3 (.A(A[2]), .B(B[2]), .CIn(n1bitadd_2_cout), .Sum(Sum[2]), .COut(n1bitadd_3_cout));
  _1BitAdd u_1bitadd_4 (.A(A[3]), .B(B[3]), .CIn(n1bitadd_3_cout), .Sum(Sum[3]), .COut(COut));
endmodule

module Inverter (
  input  [7:0] DIn,
  input  Enable,
  output [7:0] DOut
);

  xor xor_1 (DOut[0], DIn[0], Enable);
  xor xor_2 (DOut[1], DIn[1], Enable);
  xor xor_3 (DOut[2], DIn[2], Enable);
  xor xor_4 (DOut[3], DIn[3], Enable);
  xor xor_5 (DOut[4], DIn[4], Enable);
  xor xor_6 (DOut[5], DIn[5], Enable);
  xor xor_7 (DOut[6], DIn[6], Enable);
  xor xor_8 (DOut[7], DIn[7], Enable);
endmodule

module _16RAM (
  input  Clock,
  input  [7:0] Data_In,
  input  Write,
  input  [3:0] Address,
  input  Enable,
  output [7:0] BusOut,
  output [7:0] out_7,
  output [7:0] out_8,
  output [7:0] out_9,
  output [7:0] out_10,
  output [7:0] out_11,
  output [7:0] out_12,
  output [7:0] out_13,
  output [7:0] out_14,
  output [7:0] out_15,
  output [7:0] out_16,
  output [7:0] out_17,
  output [7:0] out_18,
  output [7:0] out_19,
  output [7:0] out_20,
  output [7:0] out_21,
  output [7:0] out_22
);

  wire Enable_adr0, Enable_adr1, Enable_adr2, Enable_adr3, Enable_adr4, Enable_adr5, Enable_adr6,
       Enable_adr7, Enable_adr8, Enable_adr9, Enable_adr10, Enable_adr11, Enable_adr12, Enable_adr13,
       Enable_adr14, Enable_adr15, Write_adr0, Write_adr1, Write_adr2, Write_adr3, Write_adr4, Write_adr5,
       Write_adr6, Write_adr7, Write_adr8, Write_adr9, Write_adr10, Write_adr11, Write_adr12, Write_adr13,
       Write_adr14, Write_adr15;
  wire [7:1] not_1_out;

  not not_1 (not_1_out[1], Address[0]);
  not not_2 (not_1_out[3], Address[1]);
  not not_3 (not_1_out[5], Address[2]);
  not not_4 (not_1_out[7], Address[3]);
  RAMRouter u_Write (
    .Address({not_1_out[7], Address[3], not_1_out[5], Address[2], not_1_out[3], Address[1], not_1_out[1], Address[0]}),
    .Enable(Write), .ADR0(Write_adr0), .ADR1(Write_adr1), .ADR2(Write_adr2), .ADR3(Write_adr3),
    .ADR4(Write_adr4), .ADR5(Write_adr5), .ADR6(Write_adr6), .ADR7(Write_adr7), .ADR8(Write_adr8),
    .ADR9(Write_adr9), .ADR10(Write_adr10), .ADR11(Write_adr11), .ADR12(Write_adr12), .ADR13(Write_adr13),
    .ADR14(Write_adr14), .ADR15(Write_adr15));
  RAMRouter u_Enable (
    .Address({not_1_out[7], Address[3], not_1_out[5], Address[2], not_1_out[3], Address[1], not_1_out[1], Address[0]}),
    .Enable(Enable), .ADR0(Enable_adr0), .ADR1(Enable_adr1), .ADR2(Enable_adr2), .ADR3(Enable_adr3),
    .ADR4(Enable_adr4), .ADR5(Enable_adr5), .ADR6(Enable_adr6), .ADR7(Enable_adr7), .ADR8(Enable_adr8),
    .ADR9(Enable_adr9), .ADR10(Enable_adr10), .ADR11(Enable_adr11), .ADR12(Enable_adr12),
    .ADR13(Enable_adr13), .ADR14(Enable_adr14), .ADR15(Enable_adr15));
  _8REG _0 (.Clock(Clock), .Load(Write_adr0), .Data(Data_In), .Enable(Enable_adr0), .LEDOut(out_7), .DOut(BusOut));
  _8REG _1 (.Clock(Clock), .Load(Write_adr1), .Data(Data_In), .Enable(Enable_adr1), .LEDOut(out_9), .DOut(BusOut));
  _8REG _2 (.Clock(Clock), .Load(Write_adr2), .Data(Data_In), .Enable(Enable_adr2), .LEDOut(out_11), .DOut(BusOut));
  _8REG _3 (.Clock(Clock), .Load(Write_adr3), .Data(Data_In), .Enable(Enable_adr3), .LEDOut(out_13), .DOut(BusOut));
  _8REG _4 (.Clock(Clock), .Load(Write_adr4), .Data(Data_In), .Enable(Enable_adr4), .LEDOut(out_15), .DOut(BusOut));
  _8REG _5 (.Clock(Clock), .Load(Write_adr5), .Data(Data_In), .Enable(Enable_adr5), .LEDOut(out_17), .DOut(BusOut));
  _8REG _6 (.Clock(Clock), .Load(Write_adr6), .Data(Data_In), .Enable(Enable_adr6), .LEDOut(out_19), .DOut(BusOut));
  _8REG _7 (.Clock(Clock), .Load(Write_adr7), .Data(Data_In), .Enable(Enable_adr7), .LEDOut(out_21), .DOut(BusOut));
  _8REG _8 (.Clock(Clock), .Load(Write_adr8), .Data(Data_In), .Enable(Enable_adr8), .LEDOut(out_8), .DOut(BusOut));
  _8REG _9 (.Clock(Clock), .Load(Write_adr9), .Data(Data_In), .Enable(Enable_adr9), .LEDOut(out_10), .DOut(BusOut));
  _8REG _10 (.Clock(Clock), .Load(Write_adr10), .Data(Data_In), .Enable(Enable_adr10), .LEDOut(out_12), .DOut(BusOut));
  _8REG _11 (.Clock(Clock), .Load(Write_adr11), .Data(Data_In), .Enable(Enable_adr11), .LEDOut(out_14), .DOut(BusOut));
  _8REG _12 (.Clock(Clock), .Load(Write_adr12), .Data(Data_In), .Enable(Enable_adr12), .LEDOut(out_16), .DOut(BusOut));
  _8REG _13 (.Clock(Clock), .Load(Write_adr13), .Data(Data_In), .Enable(Enable_adr13), .LEDOut(out_18), .DOut(BusOut));
  _8REG _14 (.Clock(Clock), .Load(Write_adr14), .Data(Data_In), .Enable(Enable_adr14), .LEDOut(out_20), .DOut(BusOut));
  _8REG _15 (.Clock(Clock), .Load(Write_adr15), .Data(Data_In), .Enable(Enable_adr15), .LEDOut(out_22), .DOut(BusOut));

  // Notes on the sheet:
  //   Decoder
endmodule

module RAMRouter (
  input  [7:0] Address,
  input  Enable,
  output ADR0,
  output ADR1,
  output ADR2,
  output ADR3,
  output ADR4,
  output ADR5,
  output ADR6,
  output ADR7,
  output ADR8,
  output ADR9,
  output ADR10,
  output ADR11,
  output ADR12,
  output ADR13,
  output ADR14,
  output ADR15
);

  and and_1 (ADR0, Enable, Address[1], Address[3], Address[5], Address[7]);
  and and_2 (ADR1, Enable, Address[0], Address[3], Address[5], Address[7]);
  and and_3 (ADR2, Enable, Address[1], Address[2], Address[5], Address[7]);
  and and_4 (ADR3, Enable, Address[0], Address[2], Address[5], Address[7]);
  and and_5 (ADR4, Enable, Address[1], Address[3], Address[4], Address[7]);
  and and_6 (ADR5, Enable, Address[0], Address[3], Address[4], Address[7]);
  and and_7 (ADR6, Enable, Address[1], Address[2], Address[4], Address[7]);
  and and_8 (ADR7, Enable, Address[0], Address[2], Address[4], Address[7]);
  and and_9 (ADR8, Enable, Address[1], Address[3], Address[5], Address[6]);
  and and_10 (ADR9, Enable, Address[0], Address[3], Address[5], Address[6]);
  and and_11 (ADR10, Enable, Address[1], Address[2], Address[5], Address[6]);
  and and_12 (ADR11, Enable, Address[0], Address[2], Address[5], Address[6]);
  and and_13 (ADR12, Enable, Address[1], Address[3], Address[4], Address[6]);
  and and_14 (ADR13, Enable, Address[0], Address[3], Address[4], Address[6]);
  and and_15 (ADR14, Enable, Address[1], Address[2], Address[4], Address[6]);
  and and_16 (ADR15, Enable, Address[0], Address[2], Address[4], Address[6]);
endmodule

module ProgramCounter (
  input  Enable,
  input  Load,
  input  [3:0] DIn,
  input  Count,
  input  Clock,
  input  Clear,
  output [7:0] BusOut,
  output [3:0] MonitorOut
);

  Counter #(.width(4), .max('hf)) counter_1 (
    .load(Load), .D(DIn), .count(Count), .Q(MonitorOut), .clk(Clock), .clr(Clear));  // open: carry
  assign BusOut = Enable ? {MonitorOut, MonitorOut} : 8'bz;  // Controlled_Buffer controlled_buffer_1
endmodule

module OutputDisplay (
);

  ROM rom_1 ();  // open: addr, data, sel
endmodule

module DecimalDecoder (
  input  [7:0] Data,
  output [31:0] out_2
);

  ROM #(.dataWidth(32)) rom_1 (
    .addr(Data),
    .data({out_2[31:28], out_2[15:12], out_2[27:24], out_2[11:8], out_2[23:20], out_2[7:4], out_2[19:16], out_2[3:0]}));  // open: sel

  // Notes on the sheet:
  //   contents of rom_1 (hex, n*v repeats v):
  //   e7 21 cb 6b 2d 6e ee 23 ef 2f 21e7 2121 21cb 216b 212d 216e 21ee 2123 21ef 212f cbe7 cb21 cbcb cb6b
  //   cb2d cb6e cbee cb23 cbef cb2f 6be7 6b21 6bcb 6b6b 6b2d 6b6e 6bee 6b23 6bef 6b2f 2de7 2d21 2dcb 2d6b
  //   2d2d 2d6e 2dee 2d23 2def 2d2f 6ee7 6e21 6ecb 6e6b 6e2d 6e6e 6eee 6e23 6eef 6e2f eee7 ee21 eecb ee6b
  //   ee2d ee6e eeee ee23 eeef ee2f 23e7 2321 23cb 236b 232d 236e 23ee 2323 23ef 232f efe7 ef21 efcb ef6b
  //   ef2d ef6e efee ef23 efef ef2f 2fe7 2f21 2fcb 2f6b 2f2d 2f6e 2fee 2f23 2fef 2f2f 21e7e7 21e721 21e7cb
  //   21e76b 21e72d 21e76e 21e7ee 21e723 21e7ef 21e72f 2121e7 212121 2121cb 21216b 21212d 21216e 2121ee
  //   212123 2121ef 21212f 21cbe7 21cb21 21cbcb 21cb6b 21cb2d 21cb6e 21cbee 21cb23 21cbef 21cb2f 216be7
  //   216b21 216bcb 216b6b 216b2d 216b6e 216bee 216b23 216bef 216b2f 212de7 212d21 212dcb 212d6b 212d2d
  //   212d6e 212dee 212d23 212def 212d2f 216ee7 216e21 216ecb 216e6b 216e2d 216e6e 216eee 216e23 216eef
  //   216e2f 21eee7 21ee21 21eecb 21ee6b 21ee2d 21ee6e 21eeee 21ee23 21eeef 21ee2f 2123e7 212321 2123cb
  //   21236b 21232d 21236e 2123ee 212323 2123ef 21232f 21efe7 21ef21 21efcb 21ef6b 21ef2d 21ef6e 21efee
  //   21ef23 21efef 21ef2f 212fe7 212f21 212fcb 212f6b 212f2d 212f6e 212fee 212f23 212fef 212f2f cbe7e7
  //   cbe721 cbe7cb cbe76b cbe72d cbe76e cbe7ee cbe723 cbe7ef cbe72f cb21e7 cb2121 cb21cb cb216b cb212d
  //   cb216e cb21ee cb2123 cb21ef cb212f cbcbe7 cbcb21 cbcbcb cbcb6b cbcb2d cbcb6e cbcbee cbcb23 cbcbef
  //   cbcb2f cb6be7 cb6b21 cb6bcb cb6b6b cb6b2d cb6b6e cb6bee cb6b23 cb6bef cb6b2f cb2de7 cb2d21 cb2dcb
  //   cb2d6b cb2d2d cb2d6e cb2dee cb2d23 cb2def cb2d2f cb6ee7 cb6e21 cb6ecb cb6e6b cb6e2d cb6e6e
endmodule

module CPU (
  input  [3:0] InstructionCounter,
  input  [3:0] InstructionIn,
  output [31:0] out_3
);

  ROM #(.dataWidth(32)) rom_1 (.addr({InstructionIn, InstructionCounter}), .data(out_3));  // open: sel

  // Notes on the sheet:
  //   contents of rom_1 (hex, n*v repeats v):
  //   2002 10001 100020 a0008 100020 a0008 100020 a0008 100020 a0008 100020 a0008 100020 a0008 100020
  //   a0008 2002 10001 100020 a0008 100020 a0008 100020 a0008 100020 a0008 100020 a0008 100020 a0008
  //   100020 a0008 2002 10001 100020 a0008 100020 a0008 500020 4000 40006 7*0 200021 10804 2020 40006 12*0
  //   200021 10204 880 2020 40006 11*0 200021 11400 2020 40006 12*0 600021 44006 14*0 200021 10408 2020
  //   40006 12*0 200021 810004 2020 40006 12*0 200021 1010004 2020 40006 12*0 200021 10108 2020 40006 12*0
  //   200021 2010004 4000020 400010 44006 59*0 8000 8000 8000
endmodule

module HDD (
  input  [7:0] AddressIn,
  input  Enable,
  output [7:0] out_3
);
endmodule

module RAMContents (
  input  [3:0] DataIn,
  input  Enable,
  output [7:0] out_3
);

  wire [7:0] rom_1_data;

  assign out_3 = Enable ? rom_1_data : 8'bz;  // Controlled_Buffer controlled_buffer_1
  ROM #(.addrWidth(4)) rom_1 (.addr(DataIn), .data(rom_1_data));  // open: sel
endmodule

module IFUnit (
  input  Clock,
  input  RoutWrite,
  input  [7:0] DataIn,
  input  CandWrite,
  input  CompWrite,
  input  IfOut,
  output [7:0] AddrOut
);

  wire and_1_out, not_1_out, not_2_out, not_3_out, not_4_out, not_5_out, not_6_out, not_7_out, not_8_out,
       not_9_out, xor_1_out, xor_2_out, xor_3_out, xor_4_out, xor_5_out, xor_6_out, xor_7_out, xor_8_out;
  wire [3:0] controlled_buffer_1_out;
  wire [7:0] CandidateReg_ledout, ComparisonReg_ledout, RoutingReg_ledout;

  _8REG RoutingReg (.Clock(Clock), .Load(RoutWrite), .Data(DataIn), .LEDOut(RoutingReg_ledout));  // open: Enable, DOut
  _8REG CandidateReg (
    .Clock(Clock), .Load(CandWrite), .Data(DataIn), .LEDOut(CandidateReg_ledout));  // open: Enable, DOut
  _8REG ComparisonReg (
    .Clock(Clock), .Load(CompWrite), .Data(DataIn), .LEDOut(ComparisonReg_ledout));  // open: Enable, DOut
  not not_1 (not_1_out, xor_1_out);
  xor xor_1 (xor_1_out, CandidateReg_ledout[0], ComparisonReg_ledout[0]);
  not not_2 (not_2_out, xor_2_out);
  xor xor_2 (xor_2_out, CandidateReg_ledout[1], ComparisonReg_ledout[1]);
  not not_3 (not_3_out, xor_3_out);
  xor xor_3 (xor_3_out, CandidateReg_ledout[2], ComparisonReg_ledout[2]);
  xor xor_4 (xor_4_out, CandidateReg_ledout[3], ComparisonReg_ledout[3]);
  not not_4 (not_4_out, xor_4_out);
  not not_5 (not_5_out, xor_5_out);
  xor xor_5 (xor_5_out, CandidateReg_ledout[4], ComparisonReg_ledout[4]);
  not not_6 (not_6_out, xor_6_out);
  xor xor_6 (xor_6_out, CandidateReg_ledout[5], ComparisonReg_ledout[5]);
  xor xor_7 (xor_7_out, CandidateReg_ledout[6], ComparisonReg_ledout[6]);
  not not_7 (not_7_out, xor_7_out);
  xor xor_8 (xor_8_out, CandidateReg_ledout[7], ComparisonReg_ledout[7]);
  not not_8 (not_8_out, xor_8_out);
  assign controlled_buffer_1_out = not_9_out ? RoutingReg_ledout[3:0] : 4'bz;  // Controlled_Buffer controlled_buffer_1
  assign controlled_buffer_1_out = and_1_out ? RoutingReg_ledout[7:4] : 4'bz;  // Controlled_Buffer controlled_buffer_2
  not not_9 (not_9_out, and_1_out);
  and and_1 (and_1_out, not_1_out, not_2_out, not_3_out, not_4_out, not_5_out, not_6_out, not_7_out, not_8_out);
  assign AddrOut = IfOut ? {controlled_buffer_1_out, controlled_buffer_1_out} : 8'bz;  // Controlled_Buffer controlled_buffer_3
endmodule

module OverflowReg (
  input  Write,
  input  Enable,
  input  Clock,
  input  [7:0] AddrIn,
  input  Overflow,
  output [7:0] AddrOut
);

  wire and_1_out, not_1_out;
  wire [3:0] n8reg_1_ledout, n8reg_1_ledout_2;
  wire [7:0] controlled_buffer_1_out;

  and and_1 (and_1_out, 1'b1, Overflow);
  _8REG u_8reg_1 (
    .Clock(Clock), .Load(Write), .Data(AddrIn), .LEDOut({n8reg_1_ledout, n8reg_1_ledout_2}));  // open: Enable, DOut
  assign controlled_buffer_1_out = not_1_out ? {n8reg_1_ledout_2, n8reg_1_ledout_2} : 8'bz;  // Controlled_Buffer controlled_buffer_1
  not not_1 (not_1_out, and_1_out);
  assign controlled_buffer_1_out = and_1_out ? {n8reg_1_ledout, n8reg_1_ledout} : 8'bz;  // Controlled_Buffer controlled_buffer_2
  assign AddrOut = Enable ? controlled_buffer_1_out : 8'bz;  // Controlled_Buffer controlled_buffer_3
endmodule
